// Logisim project alu.circ as structural Verilog: 4 circuits, main circuit ALU
module ALU (
  input  [7:0] a,
  input  [7:0] b,
  input  [2:0] func,
  output v,
  output c,
  output n,
  output z,
  output [7:0] result
);

  wire func000_001_cout, func000_001_cout6, or_1_out, xor_1_out;
  wire [7:0] func000_001_sum, func010_out, func011_out, func100_out, func101_out;

  assign func010_out = a & b;  // AND_Gate func010, 8 bits wide
  assign func011_out = a | b;  // OR_Gate func011, 8 bits wide
  assign func101_out = ~a;  // NOT_Gate func101, 8 bits wide
  assign func100_out = a ^ b;  // XOR_Gate func100, 8 bits wide
  ADD_SUB func000_001 (
    .a(a), .b(b), .sub(func[0]), .Cout(func000_001_cout), .sum(func000_001_sum), .Cout6(func000_001_cout6));
  xor xor_1 (xor_1_out, func000_001_cout6, func000_001_cout);
  Multiplexer #(.select(3), .width(8)) multiplexer_1 (
    .in0(func000_001_sum), .in1(func000_001_sum), .in2(func010_out), .in3(func011_out), .in4(func100_out),
    .in5(func101_out), .in6({a[6:0], 1'b0}), .in7({1'b0, a[7:1]}), .out({n, result[6:0]}), .sel(func));
  Multiplexer #(.select(3)) multiplexer_2 (
    .in0(xor_1_out), .in1(xor_1_out), .in2(1'b0), .in3(1'b0), .in4(1'b0), .in5(1'b0), .in6(1'b0), .in7(1'b0),
    .out(v), .sel(func));
  Multiplexer #(.select(3)) multiplexer_3 (
    .in0(func000_001_cout), .in1(func000_001_cout), .in2(1'b0), .in3(1'b0), .in4(1'b0), .in5(1'b0),
    .in6(a[7]), .in7(a[0]), .out(c), .sel(func));
  or or_1 (or_1_out, result[0], result[1], result[2], result[3], result[4], result[5], result[6], n);
  not not_1 (z, or_1_out);

  assign result[7] = n;

  // Notes on the sheet:
  //   func110
  //   func111
  //   Cout
  //   Cout
endmodule

module FullAdder1 (
  input  b,
  input  a,
  input  cin,
  output cout,
  output s
);

  wire and_1_out, and_2_out, xor_1_out;

  and and_1 (and_1_out, b, a);
  xor xor_1 (xor_1_out, b, a);
  xor xor_2 (s, xor_1_out, cin);
  and and_2 (and_2_out, xor_1_out, cin);
  or or_1 (cout, and_1_out, and_2_out);
endmodule

module FullAdder8 (
  input  [7:0] b,
  input  [7:0] a,
  input  cin,
  output cout,
  output [7:0] sum,
  output cout6
);

  wire bit0_cout, bit1_cout, bit2_cout, bit3_cout, bit4_cout, bit5_cout;

  FullAdder1 bit0 (.b(b[0]), .a(a[0]), .cin(cin), .cout(bit0_cout), .s(sum[0]));
  FullAdder1 bit4 (.b(b[4]), .a(a[4]), .cin(bit3_cout), .cout(bit4_cout), .s(sum[4]));
  FullAdder1 bit1 (.b(b[1]), .a(a[1]), .cin(bit0_cout), .cout(bit1_cout), .s(sum[1]));
  FullAdder1 bit5 (.b(b[5]), .a(a[5]), .cin(bit4_cout), .cout(bit5_cout), .s(sum[5]));
  FullAdder1 bit2 (.b(b[2]), .a(a[2]), .cin(bit1_cout), .cout(bit2_cout), .s(sum[2]));
  FullAdder1 bit6 (.b(b[6]), .a(a[6]), .cin(bit5_cout), .cout(cout6), .s(sum[6]));
  FullAdder1 bit3 (.b(b[3]), .a(a[3]), .cin(bit2_cout), .cout(bit3_cout), .s(sum[3]));
  FullAdder1 bit7 (.b(b[7]), .a(a[7]), .cin(cout6), .cout(cout), .s(sum[7]));
endmodule

module ADD_SUB (
  input  [7:0] a,
  input  [7:0] b,
  input  sub,
  output Cout,
  output [7:0] sum,
  output Cout6
);

  wire [7:0] multiplexer_1_out, not_1_out;

  Multiplexer #(.width(8)) multiplexer_1 (.in0(b), .in1(not_1_out), .out(multiplexer_1_out), .sel(sub));
  assign not_1_out = ~b;  // NOT_Gate not_1, 8 bits wide
  FullAdder8 fulladder8_1 (.b(a), .a(multiplexer_1_out), .cin(sub), .cout(Cout), .sum(sum), .cout6(Cout6));
endmodule
