// Logisim project cpu.circ as structural Verilog: 2 circuits, main circuit ControlUnit
module ControlUnit (
  input  [3:0] Opcode,
  input  Z,
  input  N,
  input  C,
  input  V,
  output FLAG_WE,
  output Register_WE,
  output RAM_WE,
  output ProgCount_Load,
  output STOP,
  output [1:0] outputDevice
);

  wire and_1_out, nor_1_out, not_1_out, not_2_out;

  nor nor_1 (nor_1_out, Opcode[2], Opcode[3]);
  and and_1 (and_1_out, Opcode[0], Opcode[1]);
  and and_2 (FLAG_WE, nor_1_out, not_1_out);
  not not_1 (not_1_out, and_1_out);
  Multiplexer #(.select(4)) multiplexer_1 (
    .in0(1'b1), .in1(1'b1), .in2(1'b1), .in3(1'b1), .in4(1'b1), .in5(1'b0), .in6(1'b0), .in7(1'b0),
    .in8(1'b0), .in9(1'b0), .in10(1'b0), .in11(1'b0), .in12(1'b0), .in13(1'b0), .in14(1'b0), .in15(1'b0),
    .out(Register_WE), .sel(Opcode));
  and and_3 (RAM_WE, Opcode[0], ~Opcode[1], Opcode[2], ~Opcode[3]);  // AND_Gate
  not not_2 (not_2_out, Z);
  Multiplexer #(.select(4)) multiplexer_2 (
    .in0(1'b0), .in1(1'b0), .in2(1'b0), .in3(1'b0), .in4(1'b0), .in5(1'b0), .in6(1'b1), .in7(Z),
    .in8(not_2_out), .in9(N), .in10(V), .in11(C), .in12(1'b0), .in13(1'b0), .in14(1'b0), .in15(1'b0),
    .out(ProgCount_Load), .sel(Opcode));
  and and_4 (STOP, Opcode[0], Opcode[1], Opcode[2], Opcode[3]);
  Multiplexer #(.select(4), .width(2)) multiplexer_3 (
    .in0(2'b01), .in1(2'b01), .in2(2'b01), .in3(2'b10), .in4(2'b11), .in5(2'b00), .in6(2'b00), .in7(2'b00),
    .in8(2'b00), .in9(2'b00), .in10(2'b00), .in11(2'b00), .in12(2'b00), .in13(2'b00), .in14(2'b00),
    .in15(2'b00), .out(outputDevice), .sel(Opcode));

  // Other names for the same wires on the sheet: OPC[3:0] = Opcode
endmodule

module main (
  input  RESET
);

  wire and_1_out, ArithLogUnit_c, ArithLogUnit_n, ArithLogUnit_v, ArithLogUnit_z, CLK, FLAGS_Registers_c_out,
       FLAGS_Registers_n_out, FLAGS_Registers_v_out, FLAGS_Registers_z_out, not_1_out, not_2_out,
       OPCDecoder_flag_we, OPCDecoder_progcount_load, or_1_out, or_2_out, RAM_WE, REGS_WE, STOP;
  wire [1:0] OutputDevice;
  wire [3:0] OPC;
  wire [7:0] ALU_out, main_regs_1_out1, main_regs_1_out2, multiplexer_1_out, multiplexer_2_out,
       multiplexer_3_out, RAM_out;
  wire [11:0] ADDR12, programcounter_1_line;

  Clock u_CLK (.out(CLK));
  and and_1 (and_1_out, ~STOP, CLK);  // AND_Gate
  or or_1 (or_1_out, and_1_out, RESET);
  ROM #(.addrWidth(12), .dataWidth(16)) rom_1 (.addr(programcounter_1_line), .data({OPC, ADDR12}));
  programCounter programcounter_1 (
    .CLK(or_1_out), .Jump_Addr(ADDR12), .PC_Load(OPCDecoder_progcount_load), .Reset(RESET),
    .Line(programcounter_1_line));
  not not_1 (not_1_out, OPC[3]);
  Multiplexer #(.width(8)) multiplexer_1 (
    .in0(main_regs_1_out1), .in1(main_regs_1_out2), .out(multiplexer_1_out), .sel(not_1_out));
  Multiplexer #(.select(2), .width(8)) multiplexer_2 (
    .in0({8{1'b0}}), .in1(ALU_out), .in2({{3{ADDR12[5]}}, ADDR12[4:0]}), .in3(RAM_out),
    .out(multiplexer_2_out), .sel(OutputDevice));
  not not_2 (not_2_out, RAM_WE);
  ControlUnit OPCDecoder (
    .Opcode(OPC), .Z(FLAGS_Registers_z_out), .N(FLAGS_Registers_n_out), .C(FLAGS_Registers_c_out),
    .V(FLAGS_Registers_v_out), .FLAG_WE(OPCDecoder_flag_we), .Register_WE(REGS_WE), .RAM_WE(RAM_WE),
    .ProgCount_Load(OPCDecoder_progcount_load), .STOP(STOP), .outputDevice(OutputDevice));
  main_regs main_regs_1 (
    .CLK(CLK), .WE(REGS_WE), .Rd(ADDR12[11:9]), .Rs1(ADDR12[8:6]), .Rs2(ADDR12[5:3]),
    .Data(multiplexer_2_out), .Out1(main_regs_1_out1), .Out2(main_regs_1_out2));
  RAM #(.asyncread("true")) ram_1 (
    .addr(multiplexer_1_out), .we(RAM_WE), .oe(not_2_out), .clk(CLK), .din(main_regs_1_out1), .dout(RAM_out));
  Multiplexer #(.width(8)) multiplexer_3 (
    .in0(main_regs_1_out2), .in1({{3{ADDR12[5]}}, ADDR12[4:0]}), .out(multiplexer_3_out), .sel(or_2_out));
  or or_2 (or_2_out, OPC[0], OPC[1], OPC[2], OPC[3]);
  ALU ArithLogUnit (
    .a(main_regs_1_out1), .b(multiplexer_3_out), .func(ADDR12[2:0]), .v(ArithLogUnit_v), .c(ArithLogUnit_c),
    .n(ArithLogUnit_n), .z(ArithLogUnit_z), .result(ALU_out));
  FLAGS_regs FLAGS_Registers (
    .CLK(CLK), .WE(OPCDecoder_flag_we), .Z_in(ArithLogUnit_z), .N_in(ArithLogUnit_n), .C_in(ArithLogUnit_c),
    .V_in(ArithLogUnit_v), .Z_out(FLAGS_Registers_z_out), .N_out(FLAGS_Registers_n_out),
    .C_out(FLAGS_Registers_c_out), .V_out(FLAGS_Registers_v_out));

  // Other names for the same wires on the sheet: FUNC[2:0] = ADDR12[2:0]; IMM6[5:0] = ADDR12[5:0];
  //   IMM8[7:0] = {{3{ADDR12[5]}}, ADDR12[4:0]}; Rs2[2:0] = ADDR12[5:3]; Rs1[2:0] = ADDR12[8:6];
  //   Rd[2:0] = ADDR12[11:9]

  // Notes on the sheet:
  //   sign-extender
  //   contents of rom_1 (hex, n*v repeats v):
  //   3208 5040 4600 f000
  //   OPC
  //   output mux logic
endmodule
