// Logisim project memoryProgramCounter.circ as structural Verilog: 3 circuits, main circuit programCounter
module programCounter (
  input  CLK,
  input  [11:0] Jump_Addr,
  input  PC_Load,
  input  Reset,
  output [11:0] Line
);

  wire and_1_out, fulladder1_1_cout, fulladder1_2_cout, fulladder1_3_cout, fulladder8_1_cout;
  wire [11:0] fulladder8_1_sum, multiplexer_1_out;

  Register #(.width(12)) register_1 (.D(multiplexer_1_out), .en(CLK), .clk(CLK), .Q(Line), .clr(and_1_out));
  Multiplexer #(.width(12)) multiplexer_1 (
    .in0(fulladder8_1_sum), .in1(Jump_Addr), .out(multiplexer_1_out), .sel(PC_Load));
  and and_1 (and_1_out, CLK, Reset);
  FullAdder8 fulladder8_1 (
    .b(Line[7:0]), .cin(1'b1), .cout(fulladder8_1_cout), .sum(fulladder8_1_sum[7:0]));  // open: a, cout6
  FullAdder1 fulladder1_1 (
    .a(Line[8]), .cin(fulladder8_1_cout), .cout(fulladder1_1_cout), .s(fulladder8_1_sum[8]));  // open: b
  FullAdder1 fulladder1_2 (
    .a(Line[9]), .cin(fulladder1_1_cout), .cout(fulladder1_2_cout), .s(fulladder8_1_sum[9]));  // open: b
  FullAdder1 fulladder1_3 (
    .a(Line[10]), .cin(fulladder1_2_cout), .cout(fulladder1_3_cout), .s(fulladder8_1_sum[10]));  // open: b
  FullAdder1 fulladder1_4 (.a(Line[11]), .cin(fulladder1_3_cout), .s(fulladder8_1_sum[11]));  // open: b, cout
endmodule

module instructionROM (
  input  CLK,
  input  [11:0] Jump_Addr,
  input  PC_Load,
  input  Reset,
  output [15:0] Instruction
);

  wire [11:0] programcounter_1_line;

  ROM #(.addrWidth(12), .dataWidth(16)) ProgramMemory (.addr(programcounter_1_line), .data(Instruction));
  programCounter programcounter_1 (
    .CLK(CLK), .Jump_Addr(Jump_Addr), .PC_Load(PC_Load), .Reset(Reset), .Line(programcounter_1_line));
endmodule

module dataRAM (
  input  [7:0] Address,
  input  WE,
  input  CLK,
  input  [7:0] DataIn,
  output [7:0] DataOut
);

  RAM ram_1 (.addr(Address), .we(WE), .oe(1'b1), .clk(CLK), .din(DataIn), .dout(DataOut));
endmodule
