// Logisim project registers.circ as structural Verilog: 2 circuits, main circuit main_regs
module main_regs (
  input  CLK,
  input  WE,
  input  [2:0] Rd,
  input  [2:0] Rs1,
  input  [2:0] Rs2,
  input  [7:0] Data,
  output [7:0] Out1,
  output [7:0] Out2
);

  wire decoder_1_out0, decoder_1_out1, decoder_1_out2, decoder_1_out3, decoder_1_out4, decoder_1_out5,
       decoder_1_out6, decoder_1_out7;
  wire [7:0] r1_q, r2_q, r3_q, r4_q, r5_q, r6_q, r7_q;

  Decoder #(.select(3)) decoder_1 (
    .out0(decoder_1_out0), .out1(decoder_1_out1), .out2(decoder_1_out2), .out3(decoder_1_out3),
    .out4(decoder_1_out4), .out5(decoder_1_out5), .out6(decoder_1_out6), .out7(decoder_1_out7), .sel(Rd),
    .en(WE));
  Register r1 (.D(Data), .en(decoder_1_out1), .clk(CLK), .Q(r1_q));  // open: clr
  Register r2 (.D(Data), .en(decoder_1_out2), .clk(CLK), .Q(r2_q));  // open: clr
  Register r3 (.D(Data), .en(decoder_1_out3), .clk(CLK), .Q(r3_q));  // open: clr
  Register r4 (.D(Data), .en(decoder_1_out4), .clk(CLK), .Q(r4_q));  // open: clr
  Register r5 (.D(Data), .en(decoder_1_out5), .clk(CLK), .Q(r5_q));  // open: clr
  Register r6 (.D(Data), .en(decoder_1_out6), .clk(CLK), .Q(r6_q));  // open: clr
  Register r7 (.D(Data), .en(decoder_1_out7), .clk(CLK), .Q(r7_q));  // open: clr
  Multiplexer #(.select(3), .width(8)) multiplexer_1 (
    .in0({8{1'b0}}), .in1(r1_q), .in2(r2_q), .in3(r3_q), .in4(r4_q), .in5(r5_q), .in6(r6_q), .in7(r7_q),
    .out(Out1), .sel(Rs1));
  Multiplexer #(.select(3), .width(8)) multiplexer_2 (
    .in0({8{1'b0}}), .in1(r1_q), .in2(r2_q), .in3(r3_q), .in4(r4_q), .in5(r5_q), .in6(r6_q), .in7(r7_q),
    .out(Out2), .sel(Rs2));

  // Other names for the same wires on the sheet: clock = CLK

  // Notes on the sheet:
  //   dead end b/c r0 hardwired to 0
  //   r0
endmodule

module FLAGS_regs (
  input  CLK,
  input  WE,
  input  Z_in,
  input  N_in,
  input  C_in,
  input  V_in,
  output Z_out,
  output N_out,
  output C_out,
  output V_out
);

  Register #(.width(4)) register_1 (
    .D({V_in, C_in, N_in, Z_in}), .en(WE), .clk(CLK), .Q({V_out, C_out, N_out, Z_out}));  // open: clr
endmodule
